// Logisim project alu.circ as structural Verilog: 1 circuit, main circuit alu
module alu (
  input  [31:0] A,
  input  [31:0] B,
  input  [3:0] ALUSel,
  output [31:0] Result
);

  wire adder_1_cout, adder_2_cout, comparator_1_lt;
  wire [4:0] bit_extender_3_out, bit_extender_4_out, bit_extender_5_out;
  wire [31:0] add0, adder_3_out, adder_5_out, and1, bit_extender_1_out, bit_extender_2_out, divu8, mul10,
       mulh14, mulhu11, multiplier_1_cout, multiplier_1_out, multiplier_2_cout, multiplier_2_out,
       multiplier_3_cout, negator_1_out, negator_2_out, negator_3_out, negator_4_out, not_1_out, not_2_out,
       not_3_out, not_4_out, or2, remu9, sll6, slt7, sra5, srl4, sub12, xor3;

  Negator #(.width(32)) negator_1 (.in(B), .out(negator_1_out));
  Negator #(.width(32)) negator_2 (.in(A), .out(negator_2_out));
  Negator #(.width(32)) negator_3 (.in(A), .out(negator_3_out));
  Negator #(.width(32)) negator_4 (.in(B), .out(negator_4_out));
  Multiplier #(.width(32)) multiplier_1 (
    .a(negator_2_out), .b(B), .out(multiplier_1_out), .cout(multiplier_1_cout));  // open: cin
  Multiplier #(.width(32)) multiplier_2 (
    .a(negator_1_out), .b(A), .out(multiplier_2_out), .cout(multiplier_2_cout));  // open: cin
  assign not_1_out = ~multiplier_2_out;  // NOT_Gate not_1, 32 bits wide
  Multiplier #(.width(32)) multiplier_3 (
    .a(negator_3_out), .b(negator_4_out), .cout(multiplier_3_cout));  // open: out, cin
  assign not_2_out = ~multiplier_1_out;  // NOT_Gate not_2, 32 bits wide
  assign not_3_out = ~multiplier_1_cout;  // NOT_Gate not_3, 32 bits wide
  Adder #(.width(32)) adder_1 (.a(32'h1), .b(not_1_out), .cout(adder_1_cout));  // open: out, cin
  assign not_4_out = ~multiplier_2_cout;  // NOT_Gate not_4, 32 bits wide
  Adder #(.width(32)) adder_2 (.a(32'h1), .b(not_2_out), .cout(adder_2_cout));  // open: out, cin
  assign bit_extender_1_out = {{31{1'b0}}, adder_2_cout};  // Bit_Extender bit_extender_1
  assign bit_extender_2_out = {{31{1'b0}}, adder_1_cout};  // Bit_Extender bit_extender_2
  Bit_Extender #(.in_width(32), .out_width(5), .\type ("zero")) bit_extender_3 (.in(B), .out(bit_extender_3_out));
  Bit_Extender #(.in_width(32), .out_width(5), .\type ("zero")) bit_extender_4 (.in(B), .out(bit_extender_4_out));
  Bit_Extender #(.in_width(32), .out_width(5), .\type ("zero")) bit_extender_5 (.in(B), .out(bit_extender_5_out));
  Adder #(.width(32)) adder_3 (.a(bit_extender_2_out), .b(not_4_out), .out(adder_3_out));  // open: cin, cout
  Adder #(.width(32)) adder_4 (.a(A), .b(B), .out(add0));  // open: cin, cout
  assign and1 = A & B;  // AND_Gate and_1, 32 bits wide
  assign or2 = A | B;  // OR_Gate or_1, 32 bits wide
  assign xor3 = A ^ B;  // XOR_Gate xor_1, 32 bits wide
  Shifter #(.width(32), .shift("lr")) shifter_1 (.in(A), .\dist (bit_extender_3_out), .out(srl4));
  Shifter #(.width(32), .shift("ar")) shifter_2 (.in(A), .\dist (bit_extender_4_out), .out(sra5));
  Shifter #(.width(32)) shifter_3 (.in(A), .\dist (bit_extender_5_out), .out(sll6));
  Comparator #(.width(32)) comparator_1 (.a(A), .b(B), .lt(comparator_1_lt));  // open: gt, eq
  Divider #(.width(32)) divider_1 (.a(A), .b(B), .out(divu8), .rem(remu9));  // open: upper
  Multiplier #(.width(32)) multiplier_4 (.a(A), .b(B), .out(mul10), .cout(mulhu11));  // open: cin
  Subtractor #(.width(32)) subtractor_1 (.a(A), .b(B), .out(sub12));  // open: bin, bout
  Adder #(.width(32)) adder_5 (.a(bit_extender_1_out), .b(not_3_out), .out(adder_5_out));  // open: cin, cout
  assign slt7 = {{31{1'b0}}, comparator_1_lt};  // Bit_Extender bit_extender_6
  Multiplexer #(.select(2), .width(32), .enable("false")) multiplexer_1 (
    .in0(mulhu11), .in1(adder_5_out), .in2(adder_3_out), .in3(multiplier_3_cout), .out(mulh14),
    .sel({B[31], A[31]}));
  Multiplexer #(.select(4), .width(32), .enable("false")) multiplexer_2 (
    .in0(add0), .in1(and1), .in2(or2), .in3(xor3), .in4(srl4), .in5(sra5), .in6(sll6), .in7(slt7),
    .in8(divu8), .in9(remu9), .in10(mul10), .in11(mulhu11), .in12(sub12), .in13(B), .in14(mulh14),
    .out(Result), .sel(ALUSel));  // open: in15

  // Other names for the same wires on the sheet: bsel13[31:0] = B

  // Notes on the sheet:
  //   INPUTS to your circuit
  //   DON'T CHANGE THE LOCATIONS OF THE INPUTS AND OUTPUTS!
  //   OUTPUT from your circuit
endmodule
