// Logisim project control_logic.circ as structural Verilog: 1 circuit, main circuit control_logic
module control_logic (
  input  [31:0] inst,
  input  BrEq,
  input  BrLt,
  output PCSel,
  output RegWEn,
  output [2:0] ImmSel,
  output BrUn,
  output ASel,
  output BSel,
  output [3:0] ALUSel,
  output MemRW,
  output [1:0] WBSel
);

  wire add1, add2, and1, and2, and_1_out, and_2_out, and_3_out, comparator_1_eq, comparator_2_eq,
       comparator_3_eq, comparator_4_eq, comparator_5_eq, comparator_6_eq, comparator_7_eq, comparator_8_eq,
       comparator_9_eq, comparator_10_eq, comparator_11_eq, comparator_12_eq, comparator_13_eq,
       comparator_14_eq, comparator_15_eq, comparator_16_eq, comparator_17_eq, comparator_18_eq,
       comparator_19_eq, comparator_20_eq, comparator_21_eq, comparator_22_eq, comparator_23_eq,
       comparator_24_eq, comparator_25_eq, comparator_26_eq, comparator_27_eq, comparator_28_eq,
       comparator_29_eq, comparator_30_eq, comparator_31_eq, comparator_32_eq, comparator_33_eq,
       comparator_34_eq, comparator_35_eq, comparator_36_eq, comparator_37_eq, comparator_38_eq,
       comparator_39_eq, comparator_40_eq, comparator_41_eq, comparator_42_eq, comparator_43_eq,
       comparator_44_eq, comparator_45_eq, comparator_46_eq, comparator_47_eq, comparator_48_eq,
       comparator_49_eq, comparator_50_eq, comparator_51_eq, comparator_52_eq, comparator_55_eq,
       comparator_56_eq, divu1, I_type, mul1, mulh1, mulhu1, multiplexer_1_out, not_1_out, not_2_out, or1,
       or2, or_5_out, remu1, S_type, SB_type, sll1, sll2, slt1, slt2, sra1, sra2, srl1, srl2, sub1, U_type,
       xor1, xor2;

  Comparator #(.width(7), .mode("unsigned")) comparator_1 (
    .a(7'b0100011), .b(inst[6:0]), .eq(comparator_1_eq));  // open: gt, lt
  Comparator #(.width(3), .mode("unsigned")) comparator_2 (
    .a(3'b011), .b(inst[14:12]), .eq(comparator_2_eq));  // open: gt, lt
  Comparator #(.width(7), .mode("unsigned")) comparator_3 (
    .a(7'b0100011), .b(inst[6:0]), .eq(comparator_3_eq));  // open: gt, lt
  Comparator #(.width(3), .mode("unsigned")) comparator_4 (
    .a(3'b111), .b(inst[14:12]), .eq(comparator_4_eq));  // open: gt, lt
  Comparator #(.width(7), .mode("unsigned")) comparator_5 (
    .a(7'b0110011), .b(inst[6:0]), .eq(comparator_5_eq));  // open: gt, lt
  Comparator #(.width(7), .mode("unsigned")) comparator_6 (
    .a(7'b0000011), .b(inst[6:0]), .eq(comparator_6_eq));  // open: gt, lt
  Comparator #(.width(7), .mode("unsigned")) comparator_7 (
    .a(7'b0010011), .b(inst[6:0]), .eq(comparator_7_eq));  // open: gt, lt
  Comparator #(.width(7), .mode("unsigned")) comparator_8 (
    .a(7'b0010111), .b(inst[6:0]), .eq(comparator_8_eq));  // open: gt, lt
  Comparator #(.width(7), .mode("unsigned")) comparator_9 (
    .a(7'b0110111), .b(inst[6:0]), .eq(comparator_9_eq));  // open: gt, lt
  Comparator #(.width(7), .mode("unsigned")) comparator_10 (
    .a(7'b1101111), .b(inst[6:0]), .eq(comparator_10_eq));  // open: gt, lt
  Comparator #(.width(7), .mode("unsigned")) comparator_11 (
    .a(7'b1100111), .b(inst[6:0]), .eq(comparator_11_eq));  // open: gt, lt
  Comparator #(.width(7), .mode("unsigned")) comparator_12 (
    .a(7'b1100011), .b(inst[6:0]), .eq(comparator_12_eq));  // open: gt, lt
  Comparator #(.width(7), .mode("unsigned")) comparator_13 (
    .a(7'b0010111), .b(inst[6:0]), .eq(comparator_13_eq));  // open: gt, lt
  Comparator #(.width(7), .mode("unsigned")) comparator_14 (
    .a(7'b1101111), .b(inst[6:0]), .eq(comparator_14_eq));  // open: gt, lt
  Comparator #(.width(7), .mode("unsigned")) comparator_15 (
    .a(7'b0110011), .b(inst[6:0]), .eq(comparator_15_eq));  // open: gt, lt
  Comparator #(.width(3), .mode("unsigned")) comparator_16 (
    .a(3'b000), .b(inst[14:12]), .eq(comparator_16_eq));  // open: gt, lt
  Comparator #(.width(3), .mode("unsigned")) comparator_17 (
    .a(3'b001), .b(inst[14:12]), .eq(comparator_17_eq));  // open: gt, lt
  Comparator #(.width(3), .mode("unsigned")) comparator_18 (
    .a(3'b010), .b(inst[14:12]), .eq(comparator_18_eq));  // open: gt, lt
  Comparator #(.width(3), .mode("unsigned")) comparator_19 (
    .a(3'b011), .b(inst[14:12]), .eq(comparator_19_eq));  // open: gt, lt
  Comparator #(.width(3), .mode("unsigned")) comparator_20 (
    .a(3'b100), .b(inst[14:12]), .eq(comparator_20_eq));  // open: gt, lt
  Comparator #(.width(3), .mode("unsigned")) comparator_21 (
    .a(3'b101), .b(inst[14:12]), .eq(comparator_21_eq));  // open: gt, lt
  Comparator #(.width(3), .mode("unsigned")) comparator_22 (
    .a(3'b110), .b(inst[14:12]), .eq(comparator_22_eq));  // open: gt, lt
  Comparator #(.width(3), .mode("unsigned")) comparator_23 (
    .a(3'b111), .b(inst[14:12]), .eq(comparator_23_eq));  // open: gt, lt
  Comparator #(.width(7), .mode("unsigned")) comparator_24 (
    .a({7{1'b0}}), .b(inst[31:25]), .eq(comparator_24_eq));  // open: gt, lt
  Comparator #(.width(7), .mode("unsigned")) comparator_25 (
    .a(7'b0000001), .b(inst[31:25]), .eq(comparator_25_eq));  // open: gt, lt
  Comparator #(.width(7), .mode("unsigned")) comparator_26 (
    .a(7'b0100000), .b(inst[31:25]), .eq(comparator_26_eq));  // open: gt, lt
  not not_1 (not_1_out, BrLt);
  or or_1 (ASel, comparator_12_eq, comparator_13_eq, comparator_14_eq);
  and and_1 (and_1_out, comparator_1_eq, comparator_2_eq);
  and and_2 (and_2_out, comparator_3_eq, comparator_4_eq, BrLt);
  not not_2 (not_2_out, BrEq);
  Comparator #(.width(7), .mode("unsigned")) comparator_27 (
    .a(7'b1101111), .b(inst[6:0]), .eq(comparator_27_eq));  // open: gt, lt
  Comparator #(.width(7), .mode("unsigned")) comparator_28 (
    .a(7'b1100111), .b(inst[6:0]), .eq(comparator_28_eq));  // open: gt, lt
  or or_2 (MemRW, and_1_out, and_2_out);
  Comparator #(.width(7), .mode("unsigned")) comparator_29 (
    .a(7'b1100011), .b(inst[6:0]), .eq(comparator_29_eq));  // open: gt, lt
  Multiplexer #(.select(3), .enable("false")) multiplexer_1 (
    .in0(BrEq), .in1(not_2_out), .in4(BrLt), .in5(not_1_out), .in6(BrLt), .in7(not_1_out),
    .out(multiplexer_1_out), .sel(inst[14:12]));  // open: in2, in3
  or or_3 (RegWEn, comparator_5_eq, comparator_6_eq, comparator_7_eq, comparator_8_eq, comparator_9_eq, comparator_10_eq, comparator_11_eq);
  and and_3 (and_3_out, comparator_29_eq, multiplexer_1_out);
  and and_4 (add1, comparator_15_eq, comparator_16_eq, comparator_24_eq);
  and and_5 (mul1, comparator_15_eq, comparator_16_eq, comparator_25_eq);
  and and_6 (sub1, comparator_15_eq, comparator_16_eq, comparator_26_eq);
  and and_7 (sll1, comparator_15_eq, comparator_17_eq, comparator_24_eq);
  and and_8 (mulh1, comparator_15_eq, comparator_17_eq, comparator_25_eq);
  and and_9 (mulhu1, comparator_15_eq, comparator_19_eq, comparator_25_eq);
  and and_10 (slt1, comparator_15_eq, comparator_18_eq, comparator_24_eq);
  and and_11 (xor1, comparator_15_eq, comparator_20_eq, comparator_24_eq);
  and and_12 (divu1, comparator_15_eq, comparator_21_eq, comparator_25_eq);
  and and_13 (srl1, comparator_15_eq, comparator_21_eq, comparator_24_eq);
  and and_14 (sra1, comparator_15_eq, comparator_21_eq, comparator_26_eq);
  and and_15 (or1, comparator_15_eq, comparator_22_eq, comparator_24_eq);
  and and_16 (remu1, comparator_15_eq, comparator_23_eq, comparator_25_eq);
  and and_17 (and1, comparator_15_eq, comparator_23_eq, comparator_24_eq);
  or or_4 (PCSel, and_3_out, comparator_27_eq, comparator_28_eq);
  Comparator #(.width(7), .mode("unsigned")) comparator_30 (
    .a(7'b0110011), .b(inst[6:0]), .eq(comparator_30_eq));  // open: gt, lt
  not not_3 (BSel, comparator_30_eq);
  Comparator #(.width(3), .mode("unsigned")) comparator_31 (
    .a(3'b110), .b(inst[14:12]), .eq(comparator_31_eq));  // open: gt, lt
  Comparator #(.width(3), .mode("unsigned")) comparator_32 (
    .a(3'b111), .b(inst[14:12]), .eq(comparator_32_eq));  // open: gt, lt
  Comparator #(.width(7), .mode("unsigned")) comparator_33 (
    .a(7'b0110011), .b(inst[6:0]), .eq(comparator_33_eq));  // open: gt, lt
  Comparator #(.width(7), .mode("unsigned")) comparator_34 (
    .a(7'b0010011), .b(inst[6:0]), .eq(comparator_34_eq));  // open: gt, lt
  Comparator #(.width(7), .mode("unsigned")) comparator_35 (
    .a(7'b0010111), .b(inst[6:0]), .eq(comparator_35_eq));  // open: gt, lt
  Comparator #(.width(7), .mode("unsigned")) comparator_36 (
    .a(7'b0110111), .b(inst[6:0]), .eq(comparator_36_eq));  // open: gt, lt
  Comparator #(.width(7), .mode("unsigned")) comparator_37 (
    .a(7'b1101111), .b(inst[6:0]), .eq(comparator_37_eq));  // open: gt, lt
  Comparator #(.width(7), .mode("unsigned")) comparator_38 (
    .a(7'b1100111), .b(inst[6:0]), .eq(comparator_38_eq));  // open: gt, lt
  Comparator #(.width(7), .mode("unsigned")) comparator_39 (
    .a(7'b1100011), .b(inst[6:0]), .eq(comparator_39_eq));  // open: gt, lt
  or or_5 (or_5_out, comparator_31_eq, comparator_32_eq);
  or or_6 (WBSel[0], comparator_33_eq, comparator_34_eq, comparator_35_eq, comparator_36_eq);
  or or_7 (WBSel[1], comparator_37_eq, comparator_38_eq);
  Comparator #(.width(7), .mode("unsigned")) comparator_40 (
    .a(7'b0010011), .b(inst[6:0]), .eq(comparator_40_eq));  // open: gt, lt
  Comparator #(.width(3), .mode("unsigned")) comparator_41 (
    .a(3'b000), .b(inst[14:12]), .eq(comparator_41_eq));  // open: gt, lt
  Comparator #(.width(3), .mode("unsigned")) comparator_42 (
    .a(3'b001), .b(inst[14:12]), .eq(comparator_42_eq));  // open: gt, lt
  Comparator #(.width(3), .mode("unsigned")) comparator_43 (
    .a(3'b010), .b(inst[14:12]), .eq(comparator_43_eq));  // open: gt, lt
  Comparator #(.width(3), .mode("unsigned")) comparator_44 (
    .a(3'b100), .b(inst[14:12]), .eq(comparator_44_eq));  // open: gt, lt
  Comparator #(.width(3), .mode("unsigned")) comparator_45 (
    .a(3'b101), .b(inst[14:12]), .eq(comparator_45_eq));  // open: gt, lt
  Comparator #(.width(3), .mode("unsigned")) comparator_46 (
    .a(3'b110), .b(inst[14:12]), .eq(comparator_46_eq));  // open: gt, lt
  Comparator #(.width(3), .mode("unsigned")) comparator_47 (
    .a(3'b111), .b(inst[14:12]), .eq(comparator_47_eq));  // open: gt, lt
  Comparator #(.width(7), .mode("unsigned")) comparator_48 (
    .a({7{1'b0}}), .b(inst[31:25]), .eq(comparator_48_eq));  // open: gt, lt
  Comparator #(.width(7), .mode("unsigned")) comparator_49 (
    .a(7'b0100000), .b(inst[31:25]), .eq(comparator_49_eq));  // open: gt, lt
  and and_18 (BrUn, comparator_39_eq, or_5_out);
  and and_19 (add2, comparator_40_eq, comparator_41_eq);
  and and_20 (sll2, comparator_40_eq, comparator_42_eq, comparator_48_eq);
  and and_21 (slt2, comparator_40_eq, comparator_43_eq);
  and and_22 (xor2, comparator_40_eq, comparator_44_eq);
  and and_23 (srl2, comparator_40_eq, comparator_45_eq, comparator_48_eq);
  and and_24 (sra2, comparator_40_eq, comparator_45_eq, comparator_49_eq);
  and and_25 (or2, comparator_40_eq, comparator_46_eq);
  and and_26 (and2, comparator_40_eq, comparator_47_eq);
  Comparator #(.width(7), .mode("unsigned")) comparator_50 (
    .a(7'b0000011), .b(inst[6:0]), .eq(comparator_50_eq));  // open: gt, lt
  Comparator #(.width(7), .mode("unsigned")) comparator_51 (
    .a(7'b0010011), .b(inst[6:0]), .eq(comparator_51_eq));  // open: gt, lt
  Comparator #(.width(7), .mode("unsigned")) comparator_52 (
    .a(7'b1100111), .b(inst[6:0]), .eq(comparator_52_eq));  // open: gt, lt
  Comparator #(.width(7), .mode("unsigned")) comparator_53 (
    .a(7'b0100011), .b(inst[6:0]), .eq(S_type));  // open: gt, lt
  Comparator #(.width(7), .mode("unsigned")) comparator_54 (
    .a(7'b1100011), .b(inst[6:0]), .eq(SB_type));  // open: gt, lt
  Comparator #(.width(7), .mode("unsigned")) comparator_55 (
    .a(7'b0010111), .b(inst[6:0]), .eq(comparator_55_eq));  // open: gt, lt
  Comparator #(.width(7), .mode("unsigned")) comparator_56 (
    .a(7'b0110111), .b(inst[6:0]), .eq(comparator_56_eq));  // open: gt, lt
  Comparator #(.width(7), .mode("unsigned")) comparator_57 (
    .a(7'b1101111), .b(inst[6:0]), .eq(ImmSel[2]));  // open: gt, lt
  or or_8 (I_type, comparator_50_eq, comparator_51_eq, comparator_52_eq);
  or or_9 (U_type, comparator_55_eq, comparator_56_eq);
  or or_10 (ImmSel[0], S_type, U_type);
  or or_11 (ImmSel[1], SB_type, U_type);

  assign ALUSel = 4'b0000;

  // Other names for the same wires on the sheet: UJ_type = ImmSel[2]; opcode[6:0] = inst[6:0];
  //   funct3[2:0] = inst[14:12]; funct7[6:0] = inst[31:25]

  // Notes on the sheet:
  //   INPUTS to your circuit
  //   DON'T CHANGE THE LOCATIONS OF THE INPUTS AND OUTPUTS!
  //   OUTPUT from your circuit
endmodule
