// Logisim project cpu.circ as structural Verilog: 1 circuit, main circuit main
module main (
  input  [31:0] INSTRUCTION,
  input  CLOCK,
  output [31:0] PROGRAM_COUNTER,
  output [31:0] ra,
  output [31:0] sp,
  output [31:0] t0,
  output [31:0] t1,
  output [31:0] t2,
  output [31:0] s0,
  output [31:0] s1,
  output [31:0] a0
);

  wire ASel, BrEq, BrLt, BrUn, BSel, MemRW, PCSel, RegWEn;
  wire [1:0] WBSel;
  wire [2:0] ImmSel;
  wire [3:0] ALUSel;
  wire [31:0] adder_1_out, adder_2_out, ALUout, EX_INS, EX_PC, imm, MemOut, multiplexer_1_out,
       multiplexer_2_out, multiplexer_3_out, rs1, rs2, WriteBack;

  Adder #(.width(32)) adder_1 (.a(PROGRAM_COUNTER), .b(32'h4), .out(adder_1_out));  // open: cin, cout
  Multiplexer #(.width(32), .enable("false")) multiplexer_1 (
    .in0(adder_1_out), .in1(ALUout), .out(multiplexer_1_out), .sel(PCSel));
  Register #(.width(32)) PC (.D(multiplexer_1_out), .en(1'b1), .clk(CLOCK), .Q(PROGRAM_COUNTER));  // open: clr
  control_logic control_logic_1 (
    .BSel(BSel), .ASel(ASel), .BrUn(BrUn), .ImmSel(ImmSel), .RegWEn(RegWEn), .PCSel(PCSel), .BrLt(BrLt),
    .BrEq(BrEq), .inst(EX_INS), .ALUSel(ALUSel), .MemRW(MemRW), .WBSel(WBSel));
  Register #(.width(32)) IF_EX_PC (.D(PROGRAM_COUNTER), .en(1'b1), .clk(CLOCK), .Q(EX_PC));  // open: clr
  Register #(.width(32)) IF_EX_INS (.D(INSTRUCTION), .en(1'b1), .clk(CLOCK), .Q(EX_INS));  // open: clr
  imm_gen imm_gen_1 (.ImmSel(ImmSel), .imm(imm), .inst(EX_INS));
  regfile_main RegFile (
    .rs2(EX_INS[24:20]), .rd(EX_INS[11:7]), .Read_Data_1(rs1), .Read_Data_2(rs2), .ra(ra), .sp(sp), .t0(t0),
    .t1(t1), .t2(t2), .s0(s0), .s1(s1), .a0(a0), .rs1(EX_INS[19:15]), .Write_Data(WriteBack),
    .RegWEn(RegWEn), .clk(CLOCK));
  branch_comp branch_comp_1 (.BrEq(BrEq), .BrUn(BrUn), .rs1(rs1), .BrLt(BrLt), .rs2(rs2));
  Multiplexer #(.width(32), .enable("false")) multiplexer_2 (
    .in0(rs1), .in1(EX_PC), .out(multiplexer_2_out), .sel(ASel));
  Multiplexer #(.width(32), .enable("false")) multiplexer_3 (.in0(rs2), .in1(imm), .out(multiplexer_3_out), .sel(BSel));
  alu Arithmetic_Logic_Unit (.ALUSel(ALUSel), .Result(ALUout), .A(multiplexer_2_out), .B(multiplexer_3_out));
  // mem_main DMEM: pin names not known; wires that end beside it: ALUout, rs2, CLOCK, MemRW, MemOut
  Adder #(.width(32)) adder_2 (.a(32'h4), .b(EX_PC), .out(adder_2_out));  // open: cin, cout
  Multiplexer #(.select(2), .width(32), .enable("false")) multiplexer_4 (
    .in0(MemOut), .in1(ALUout), .in2(adder_2_out), .out(WriteBack), .sel(WBSel));  // open: in3

  // Other names for the same wires on the sheet: clk = CLOCK

  // Notes on the sheet:
  //   Output
  //   IMEM (do **NOT** move this)
  //   Inputs
  //   It is OK to move the PC, RegFile, ALU, MEM, Branch Comp, Imm Gen, and Control Logic to wherever is most convenient for you when constructing your CPU, and to delete this text
  //   Inputs/Outputs for testing. Do **NOT** move these.
endmodule
