// Logisim project regfile.circ as structural Verilog: 1 circuit, main circuit main
module main (
  input  [4:0] rs1,
  input  [4:0] rs2,
  input  [4:0] rd,
  input  [31:0] Write_Data,
  input  RegWEn,
  input  clk,
  output [31:0] ra,
  output [31:0] sp,
  output [31:0] t0,
  output [31:0] t1,
  output [31:0] t2,
  output [31:0] s0,
  output [31:0] s1,
  output [31:0] a0,
  output [31:0] Read_Data_1,
  output [31:0] Read_Data_2
);

  wire decoder_1_out1, decoder_1_out2, decoder_1_out5, decoder_1_out6, decoder_1_out7, decoder_1_out8,
       decoder_1_out9, decoder_1_out10;
  wire [31:0] multiplexer_1_out, multiplexer_2_out, multiplexer_3_out, multiplexer_4_out, multiplexer_5_out,
       multiplexer_6_out, multiplexer_7_out, multiplexer_8_out, x0;

  Decoder #(.select(5)) decoder_1 (
    .out1(decoder_1_out1), .out2(decoder_1_out2), .out5(decoder_1_out5), .out6(decoder_1_out6),
    .out7(decoder_1_out7), .out8(decoder_1_out8), .out9(decoder_1_out9), .out10(decoder_1_out10), .sel(rd));  // open: out0, out3, out4, out11, out12, out13, out14, out15, out16, out17, out18, out19, out20, out21, out22, out23, out24, out25, out26, out27, out28, out29, out30, out31, en
  Multiplexer #(.width(32), .enable("false")) multiplexer_1 (
    .in0(ra), .in1(Write_Data), .out(multiplexer_1_out), .sel(decoder_1_out1));
  Multiplexer #(.width(32), .enable("false")) multiplexer_2 (
    .in0(sp), .in1(Write_Data), .out(multiplexer_2_out), .sel(decoder_1_out2));
  Multiplexer #(.width(32), .enable("false")) multiplexer_3 (
    .in0(t0), .in1(Write_Data), .out(multiplexer_3_out), .sel(decoder_1_out5));
  Multiplexer #(.width(32), .enable("false")) multiplexer_4 (
    .in0(t1), .in1(Write_Data), .out(multiplexer_4_out), .sel(decoder_1_out6));
  Multiplexer #(.width(32), .enable("false")) multiplexer_5 (
    .in0(t2), .in1(Write_Data), .out(multiplexer_5_out), .sel(decoder_1_out7));
  Multiplexer #(.width(32), .enable("false")) multiplexer_6 (
    .in0(s0), .in1(Write_Data), .out(multiplexer_6_out), .sel(decoder_1_out8));
  Multiplexer #(.width(32), .enable("false")) multiplexer_7 (
    .in0(s1), .in1(Write_Data), .out(multiplexer_7_out), .sel(decoder_1_out9));
  Multiplexer #(.width(32), .enable("false")) multiplexer_8 (
    .in0(a0), .in1(Write_Data), .out(multiplexer_8_out), .sel(decoder_1_out10));
  Register #(.width(32)) register_1 (.clk(clk), .Q(x0), .clr(1'b1));  // open: D, en
  Register #(.width(32)) register_2 (.D(multiplexer_1_out), .en(RegWEn), .clk(clk), .Q(ra));  // open: clr
  Register #(.width(32)) x2 (.D(multiplexer_2_out), .en(RegWEn), .clk(clk), .Q(sp));  // open: clr
  Register #(.width(32)) x5 (.D(multiplexer_3_out), .en(RegWEn), .clk(clk), .Q(t0));  // open: clr
  Register #(.width(32)) x6 (.D(multiplexer_4_out), .en(RegWEn), .clk(clk), .Q(t1));  // open: clr
  Register #(.width(32)) x7 (.D(multiplexer_5_out), .en(RegWEn), .clk(clk), .Q(t2));  // open: clr
  Register #(.width(32)) x8 (.D(multiplexer_6_out), .en(RegWEn), .clk(clk), .Q(s0));  // open: clr
  Register #(.width(32)) x9 (.D(multiplexer_7_out), .en(RegWEn), .clk(clk), .Q(s1));  // open: clr
  Register #(.width(32)) x10 (.D(multiplexer_8_out), .en(RegWEn), .clk(clk), .Q(a0));  // open: clr
  Multiplexer #(.select(5), .width(32), .enable("false")) multiplexer_9 (
    .in0(x0), .in1(ra), .in2(sp), .in5(t0), .in6(t1), .in7(t2), .in8(s0), .in9(s1), .in10(a0),
    .out(Read_Data_1), .sel(rs1));  // open: in3, in4, in11, in12, in13, in14, in15, in16, in17, in18, in19, in20, in21, in22, in23, in24, in25, in26, in27, in28, in29, in30, in31
  Multiplexer #(.select(5), .width(32), .enable("false")) multiplexer_10 (
    .in0(x0), .in1(ra), .in2(sp), .in5(t0), .in6(t1), .in7(t2), .in8(s0), .in9(s1), .in10(a0),
    .out(Read_Data_2), .sel(rs2));  // open: in3, in4, in11, in12, in13, in14, in15, in16, in17, in18, in19, in20, in21, in22, in23, in24, in25, in26, in27, in28, in29, in30, in31

  // Other names for the same wires on the sheet: read_data1[31:0] = Read_Data_1; read_data2[31:0] = Read_Data_2;
  //   read_reg1[4:0] = rs1; read_reg2[4:0] = rs2; write_en = RegWEn; write_reg[4:0] = rd

  // Notes on the sheet:
  //   INPUTS to your circuit
  //   DON'T CHANGE THE LOCATIONS OF THE INPUTS AND OUTPUTS!
  //   These are DEBUG/TEST outputs from your circuit.
  //   OUTPUTS from your circuit
endmodule
